# Fritzing sketch Direct-Connected-Example (saved by Fritzing 0.9.3b)
breadboards: 1

parts:
  Bauteil1 = Arduino Nano (Rev3.0)
  JP1 = Header 5x2 [package=2x5-ra]
  JP2 = Header 5x2 [package=2x5-ra]
  JP3 = Header 5x2 [package=2x5-ra]

nets:
  N1: Bauteil1.D1/TX, JP2.1
  N2: Bauteil1.D0/RX, JP2.2
  N3: Bauteil1.D2, JP1.10
  N4: Bauteil1.D3, JP1.9
  N5: Bauteil1.D4, JP1.8
  N6: Bauteil1.D5, JP1.7
  N7: Bauteil1.D6, JP1.6
  N8: Bauteil1.D7, JP1.5
  N9: Bauteil1.D8, JP3.10
  N10: Bauteil1.D9, JP3.8
  N11: Bauteil1.D10, JP3.6
  N12: Bauteil1.D11/MOSI, JP3.4
  N13: Bauteil1.A5, JP2.8
  N14: Bauteil1.A4, JP2.7
  N15: Bauteil1.A3, JP2.6
  N16: Bauteil1.A2, JP2.5
  N17: Bauteil1.A1, JP2.4
  N18: Bauteil1.A0, JP2.3

notes:
  <-- Display PCB
  <-- Pin 1
  <-- Pin 2
  __________ Edge of Display PCB
